// Digital circuit dynhazard.dig as structural Verilog
module dynhazard (
  input  x1,
  input  x2,
  input  x3,
  output y
);

  wire and_1_out, and_2_out, not_1_out, or_1_out;

  or or_1 (or_1_out, x1, x2);
  and and_1 (and_1_out, x1, x3);
  not not_1 (not_1_out, x1);
  and and_2 (and_2_out, and_1_out, not_1_out);
  or or_2 (y, or_1_out, and_2_out);
endmodule
